# Fritzing sketch Basic OpAmp (saved by Fritzing 0.9.3b)
circuit board: 4.72722cm x 5.43278cm
breadboards: 1

parts:
  U2 = LM 358 Dual Op-Amp [package="DIP8 [THT]"]
  R7 = Resistor [tolerance=±5% resistance=10k package=THT]
  R8 = Resistor [tolerance=±5% resistance=10k package=THT]
  R9 = Resistor [tolerance=±5% resistance=1k package=THT]
  R10 = Resistor [tolerance=±5% resistance=10k package=THT]
  Arduino1 = Arduino Uno (Rev3)
  R11 = Photocell (LDR) [package=THT]
  Q2 = NPN-Transistor [package="TO92 [THT]"]
  R12 = Resistor [tolerance=±5% resistance=220 package=THT]
  R13 = Resistor [tolerance=±5% resistance=220 package=THT]
  LED1 = LED - 5mm [color="Red (633nm)" package="5 mm [THT]"]

nets (from the schematic view):
  N1: U2.connector0, U2.connector7, R7.Pin_1, R10.Pin_0, Q2.E, R12.Pin_1
  N2: U2.connector1, R9.Pin_1
  N3: U2.connector2, R7.Pin_0, R8.Pin_0
  N4: U2.connector3, Arduino1.GND, LED1.anode
  N5: R9.Pin_0, R10.Pin_1
  N6: R11.pin_0, Q2.B
  N7: R13.Pin_1, LED1.cathode
