# Fritzing sketch MASTER! (saved by Fritzing 0.9.3b)
breadboards: 1

parts:
  Part1 = Arduino Mega ADK (Rev3)
  R1 = PHOTOCELL [package=photocell-kit]
  R2 = Resistor [tolerance=±5% resistance=220 package=THT]
  LED1 = RGB LED - (4 legs) [package="5 mm [THT]"]
  R3 = Resistor [tolerance=±5% resistance=220 package=THT]
  R4 = Resistor [tolerance=±5% resistance=220 package=THT]
  R5 = Resistor [tolerance=±5% resistance=220 package=THT]
  R6 = PHOTOCELL [package=photocell-kit]
  R7 = Resistor [tolerance=±5% resistance=220 package=THT]
  J1 = Piezo Speaker
  J2 = Infrared Proximity Sensor
  LED2 = LED - 5mm [color="Yellow (585nm)" package="5 mm [THT]"]
  R8 = Resistor [tolerance=±5% resistance=220 package=THT]
  Part2 = Arduino Uno (Rev3)
  LED3 = LED - 5mm [color="Red (633nm)" package="5 mm [THT]"]
  LED4 = LED - 5mm [color="Blue (470nm)" package="5 mm [THT]"]
  LED5 = LED - 5mm [color="White (6500K)" package="5 mm [THT]"]
  LED6 = LED - 5mm [color="Green (560nm)" package="5 mm [THT]"]
  LED7 = LED - 5mm [color="Yellow (585nm)" package="5 mm [THT]"]
  R9 = Resistor [tolerance=±5% resistance=220 package=THT]
  R10 = Resistor [tolerance=±5% resistance=220 package=THT]
  R11 = Resistor [tolerance=±5% resistance=220 package=THT]
  R12 = Resistor [tolerance=±5% resistance=220 package=THT]
  R13 = Resistor [tolerance=±5% resistance=220 package=THT]
  J3 = Piezo Speaker

nets:
  N1: Part1.A0, R1.P$2, R2.Pin_0
  N2: Part1.A3, R6.P$2, R7.Pin_0
  N3: Part1.D10_PWM, LED2.anode
  N4: Part1.D9_PWM, J1.pin2
  5V: Part1.5V, R1.P$1, LED1.common_anode, R6.P$1, J1.pin1, J2.Vcc
  GND: Part1.GND, R2.Pin_1, J2.GND, R8.Pin_0
  N5: Part1.D0/RX0, J2.Vout
  N6: Part1.D2_PWM, R3.Pin_0
  N7: Part1.D4_PWM, R4.Pin_1
  N8: Part1.D6_PWM, R5.Pin_1
  N9: LED1.red_cathode, R3.Pin_1
  N10: LED1.green_cathode, R4.Pin_0
  N11: LED1.blue_cathode, R5.Pin_0
  N12: LED2.cathode, R8.Pin_1
  N13: Part2.GND, R9.Pin_0, R10.Pin_0, R11.Pin_0, R12.Pin_0, R13.Pin_0, J3.pin1
  N14: Part2.D0/RX, LED3.anode
  N15: Part2.D1/TX, LED7.anode
  N16: Part2.D2, LED6.anode
  N17: Part2.D3_PWM, LED4.anode
  N18: Part2.D4, LED5.anode
  N19: Part2.D5_PWM, J3.pin2
  N20: LED3.cathode, R9.Pin_1
  N21: LED4.cathode, R12.Pin_1
  N22: LED5.cathode, R13.Pin_1
  N23: LED6.cathode, R11.Pin_1
  N24: LED7.cathode, R10.Pin_1
